# Fritzing sketch uncensor (saved by Fritzing 0.9.0b)
breadboards: 1

parts:
  U1 = attiny85 [package=dip]
  SP1 = SPEAKER [package=pcb_mount_speaker]
  VCC1 = 4 x AAA Battery Mount

nets:
  N1: U1.Pin_3, SP1.-
  N2: U1.Pin_4, VCC1.-
  N3: U1.Pin_6, SP1.+
  N4: U1.Pin_8, VCC1.+
